// Digital circuit snake_circt.dig as structural Verilog
module snake_circt (
  input  clk,
  input  in_2,
  input  in_3,
  input  in_4,
  input  in_5,
  input  in_6
);

  wire notconnected_1_out, pullup_1_out;
  wire [2:0] u_verisnake_c_addr;
  wire [4:1] button_2_out;
  wire [6:0] u_seven_segment_decoder_segments;
  wire [7:0] u_verisnake_r_data, u_verisnake_score;

  Button button_1 (.out(button_2_out[1]));
  Button button_2 (.out(button_2_out[4]));
  Button button_3 (.out(button_2_out[3]));
  Button button_4 (.out(button_2_out[2]));
  PullUp pullup_1 (.out(pullup_1_out));
  Button button_5 (.out(pullup_1_out));
  verisnake #(.applicationType("IVERILOG"), .iverilogOptions("-g2012"), .CodeFile("D:\\dev\\verilogsnake\\snake.v")) u_verisnake (
    .clk(clk), .rst(pullup_1_out), .ctl({button_2_out, 1'b0}), .score(u_verisnake_score),
    .r_data(u_verisnake_r_data), .c_addr(u_verisnake_c_addr));
  seven_segment_decoder #(.applicationType("IVERILOG"), .CodeFile("C:\\Users\\neddien\\Desktop\\verilogsnake\\seven_segment_decoder.v")) u_seven_segment_decoder (
    .digit(u_verisnake_score[3:0]), .segments(u_seven_segment_decoder_segments));
  LedMatrix #(.ledPersistence("true")) ledmatrix_1 (.rows(u_verisnake_r_data), .column(u_verisnake_c_addr));
  VGA vga_1 (.R(in_2), .G(in_4), .B(in_3), .H(in_5), .V(in_6), .C(clk));
  Seven_Seg seven_seg_1 (
    .a(u_seven_segment_decoder_segments[6]), .b(u_seven_segment_decoder_segments[5]),
    .c(u_seven_segment_decoder_segments[4]), .d(u_seven_segment_decoder_segments[3]),
    .e(u_seven_segment_decoder_segments[2]), .f(u_seven_segment_decoder_segments[1]),
    .g(u_seven_segment_decoder_segments[0]), .dp(notconnected_1_out));
  // NotConnected on notconnected_1_out

  // Notes on the sheet:
  //   clk: Hz: 50
endmodule
